// Logisim project ex4.circ as structural Verilog: 5 circuits, main circuit RotRight
module RotRight (
  input  [15:0] INPUT0,
  input  [3:0] AMOUNT,
  output [15:0] OUTPUT0
);

  wire [15:0] multiplexer_1_out, multiplexer_2_out, multiplexer_3_out, rot1_1_out_2, rot2_1_out_2,
       rot4_1_out_2, rot8_1_out_2;

  rot1 rot1_1 (.out_2(rot1_1_out_2), .in_1(INPUT0));
  Multiplexer #(.enable("false"), .width(16)) multiplexer_1 (
    .in0(INPUT0), .in1(rot1_1_out_2), .out(multiplexer_1_out), .sel(AMOUNT[0]));
  rot2 rot2_1 (.out_2(rot2_1_out_2), .in_1(multiplexer_1_out));
  Multiplexer #(.enable("false"), .width(16)) multiplexer_2 (
    .in0(multiplexer_1_out), .in1(rot2_1_out_2), .out(multiplexer_2_out), .sel(AMOUNT[1]));
  Multiplexer #(.enable("false"), .width(16)) multiplexer_3 (
    .in0(multiplexer_2_out), .in1(rot4_1_out_2), .out(multiplexer_3_out), .sel(AMOUNT[2]));
  rot4 rot4_1 (.out_2(rot4_1_out_2), .in_1(multiplexer_2_out));
  Multiplexer #(.enable("false"), .width(16)) multiplexer_4 (
    .in0(multiplexer_3_out), .in1(rot8_1_out_2), .out(OUTPUT0), .sel(AMOUNT[3]));
  rot8 rot8_1 (.out_2(rot8_1_out_2), .in_1(multiplexer_3_out));

  // Other names for the same wires on the sheet: one = AMOUNT[0]; two = AMOUNT[1]; four = AMOUNT[2];
  //   eight = AMOUNT[3]
endmodule

module rot1 (
  input  [15:0] in_1,
  output [15:0] out_2
);


  assign out_2 = {in_1[0], in_1[15:1]};

  // Other names for the same wires on the sheet: Low[14:0] = in_1[15:1]; Top = in_1[0]
endmodule

module rot2 (
  input  [15:0] in_1,
  output [15:0] out_2
);


  assign out_2 = {in_1[1:0], in_1[15:2]};

  // Other names for the same wires on the sheet: Low[13:0] = in_1[15:2]; Top[1:0] = in_1[1:0]
endmodule

module rot4 (
  input  [15:0] in_1,
  output [15:0] out_2
);


  assign out_2 = {in_1[3:0], in_1[15:4]};

  // Other names for the same wires on the sheet: Low[11:0] = in_1[15:4]; Top[3:0] = in_1[3:0]
endmodule

module rot8 (
  input  [15:0] in_1,
  output [15:0] out_2
);


  assign out_2 = {in_1[7:0], in_1[15:8]};

  // Other names for the same wires on the sheet: Low[7:0] = in_1[15:8]; Top[7:0] = in_1[7:0]
endmodule
